# Fritzing sketch hedgehog-prototype (saved by Fritzing 0.9.3b)
breadboards: 1

parts:
  Part1 = Adafruit Feather HUZZAH ESP8266 [part_number="Adafruit #2821"]
  DHT1 = DHT22 Humidity and Temperature Sensor
  Part2 = Adafruit OLED FeatherWing [part_number="Adafruit #2900"]
  R1 = Resistor [tolerance=±5% resistance=16k package=THT]

nets:
  N1: Part1.CH_PD, Part2.G
  N2: Part1.TXD, Part2.TX
  N3: Part1.RXD, Part2.RX
  N4: Part1.GPIO12/MISO, DHT1.DATA, Part2.MISO, Part2.M, R1.Pin_1
  N5: Part1.GPIO13/MOSI, Part2.MOSI, Part2.L
  N6: Part1.GPIO14/SCK, Part2.SCK, Part2.N
  N7: Part1.ADC, Part2.A
  GND: Part1.GND, DHT1.GND, Part2.GND
  3.3V: Part1.3.3V, DHT1.VDD, Part2.3.3V, R1.Pin_0
  N8: Part1.RESET, Part2.!RESET
  N9: Part1.VBAT, Part2.VBAT
  N10: Part1.EN, Part2.EN
  N11: Part1.VBUS, Part2.USB
  N12: Part1.GPIO15, Part2.K
  N13: Part1.GPIO0, Part2.J
  N14: Part1.GPIO16, Part2.I
  N15: Part1.GPIO2, Part2.H
  N16: Part1.GPIO5/SCL, Part2.SCL
  N17: Part1.GPIO4/SDA, Part2.SDA

custom parts:
  Adafruit Feather HUZZAH ESP8266: his is the Adafruit Feather HUZZAH ESP8266 - our take on an 'all-in-one' ESP8266 WiFi development board with built in USB and battery charging. Its an ESP8266 WiFi module with all the extras you need, ready to rock! We have other boards in the Feather family, check'em out here. At the Feather HUZZAH's heart is an ESP8266 WiFi microcontroller clocked at 80 MHz and at 3.3V logic. This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
  Adafruit OLED FeatherWing: This is the FeatherWing OLED: it adds a 128x32 monochrome OLED plus 3 user buttons to any Feather main board. These displays are small, only about 1" diagonal, but very readable due to the high contrast of an OLED display. This screen is made of 128x32 individual white OLED pixels and because the display makes its own light, no backlight is required. This reduces the power required to run the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
